// Logisim project Test.circ as structural Verilog: 2 circuits, main circuit main
module main (
);

  wire A_Button_out, and_2_out;

  Button A_Button (.out(A_Button_out));
  AND_Gate and_1 ();  // open: in_1, in_2, out_3
  LED A_LED (.in(and_2_out));
  buf and_2 (and_2_out, A_Button_out);  // AND_Gate_part
  RAM ram_1 ();  // open: addr, data, sel, clk, ld, clr
  ROM rom_1 ();  // open: addr, data, sel
endmodule

module AND_Gate (
  input  in_1,
  input  in_2,
  output out_3
);

  and and_1 (out_3, in_1, in_2);
endmodule
